# Fritzing sketch Arduino_24hrs_Clock_Fonts_Schematics (saved by Fritzing 0.9.3b)

parts:
  ARDUINO_NANO = Arduino Nano (Rev3.0)
  MAX7219_32X8 = LED Matrix - Serial Interface - Red/Green/Blue
  Part8 = LED Matrix - Serial Interface - Red/Green/Blue  # not connected
  Part9 = LED Matrix - Serial Interface - Red/Green/Blue  # not connected
  Part10 = LED Matrix - Serial Interface - Red/Green/Blue  # not connected
  BUTTON_A = Round Pushbutton
  BUTTON_B = Round Pushbutton
  DS3231_RTC = ZS-042 RTC Module
  DC_5V = Power Jack [package=power_jack_pth_lock]
  part = Zener Diode [part_number=1N4732A breakdown_voltage=3.6V package="300 mil [THT]"]

nets:
  N1: ARDUINO_NANO.D2, BUTTON_A.leg0
  N2: ARDUINO_NANO.D3, BUTTON_B.leg0
  N3: ARDUINO_NANO.D10, MAX7219_32X8.CS
  N4: ARDUINO_NANO.D11/MOSI, MAX7219_32X8.MOSI
  GND: ARDUINO_NANO.GND, MAX7219_32X8.GND, DS3231_RTC.GND, DC_5V.GND
  5V: ARDUINO_NANO.5V, MAX7219_32X8.VCC, BUTTON_A.leg1, BUTTON_B.leg1, part.cathode
  N5: ARDUINO_NANO.A5, DS3231_RTC.SCL
  N6: ARDUINO_NANO.A4, DS3231_RTC.SDA
  N7: ARDUINO_NANO.D13/SCK, MAX7219_32X8.SCK
  N8: DS3231_RTC.VCC, DC_5V.PWR, part.anode

custom parts:
  LED Matrix - Serial Interface - Red/Green/Blue: Description: This is a large sized RGB LED Matrix with a backpack that has been designed to take SPI serial input and display any graphics you pass it. All the refreshing and communication control is taken care of by the backpack. It's even reprogrammable! 7 software selectable colors are available! Unit comes with a Red/Green/Blue LED Matrix assembled with a RGB Matrix Backpack Controller.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
  Round Pushbutton: A generic pushbutton.
  Round Pushbutton: A generic pushbutton.
  Power Jack: Power Jack This is the standard 5.5mm barrel jack for power. The PTH is the most common, proven, reliable, footprint. All others are experimental. The Slot footprint only works if the mill layer is transmitted to the PCB fab house so be warned. Spark Fun Electronics SKU : PRT-00119. Mating wall wart : TOL-00298 (and others)
